# Fritzing sketch buzzer (saved by Fritzing 0.9.4)
breadboards: 1

parts:
  Mod1 = Raspberry Pi 4B
  R1 = Resistor [tolerance=±5% resistance=100 package=THT]
  Part2 = KY-006 Passive Buzzer Module [package="Breakout board"]

nets:
  N1: Mod1.3V3, R1.Pin_1
  N2: Mod1.GND, Part2.-
  N3: Mod1.GPIO17, Part2.S

custom parts:
  KY-006 Passive Buzzer Module: Passive Piezoelectric Buzzer Module Keyes KY-006, it can produce a range of sound tones depending on the input frequency.
