# Fritzing sketch fritzing_schemat (saved by Fritzing 0.9.3b)
breadboards: 1

parts:
  LED1 = LED - 5mm [color="Red (633nm)" package="5 mm [THT]"]  # not connected
  Mod1 = Raspberry Pi 4B
  R1 = Resistor [tolerance=±5% resistance=100 package=THT]  # not connected
  J1 = Piezo Speaker  # not connected
  Part1 = Logic Level Converter
  T2 = TMP36 Temperature Sensor [package="TO92 [THT]"]  # not connected
  J2 = Basic Servo

nets:
  N1: Mod1.3V3, Part1.LV
  5V: Mod1.5V, Part1.HV, J2.vcc
  GND: Mod1.GND, Part1.GND, J2.gnd
  N2: Mod1.GPIO17, Part1.TX2_LV
  N3: Part1.TX2_HV, J2.pulse
