# Fritzing sketch servo (saved by Fritzing 0.9.4)
breadboards: 1

parts:
  Mod1 = Raspberry Pi 4B
  Part1 = Logic Level Converter
  J1 = Basic Servo

nets:
  N1: Mod1.3V3, Part1.LV
  5V: Mod1.5V, Part1.HV, J1.vcc
  GND: Mod1.GND, Part1.GND, J1.gnd
  N2: Mod1.GPIO17, Part1.TX2_LV
  N3: Part1.TX2_HV, J1.pulse
