# Fritzing sketch schemat (saved by Fritzing 0.9.10b)
breadboards: 1

parts:
  Mod1 = Raspberry Pi 4B
  Part1 = Logic Level Converter
  J1 = Basic Servo
  Part2 = Adafruit VL530X Time of Flight Distance Sensor [part_number="Adafruit #3317"]
  R1 = Resistor [tolerance=±5% power=0.25 resistance=220 package=THT]
  R2 = Resistor [tolerance=±5% power=0.25 resistance=220 package=THT]
  R3 = Resistor [tolerance=±5% power=0.25 resistance=220 package=THT]

nets:
  3V3: Mod1.3V3, Part1.LV, Part2.VCC, R1.Pin_1, R2.Pin_1, R3.Pin_1
  5V: Mod1.5V, Part1.HV, J1.vcc
  N1: Mod1.GPIO2, Part2.SCL, R1.Pin_0
  N2: Mod1.GPIO3, Part2.SDA, R2.Pin_0
  GND: Mod1.GND, Part1.GND, J1.gnd, Part2.GND
  N3: Mod1.GPIO18, Part1.TX2_LV
  N4: Part1.TX2_HV, J1.pulse
  N5: Part2.XSHUT, R3.Pin_0

custom parts:
  Adafruit VL530X Time of Flight Distance Sensor: The VL53L0X is a Time of Flight distance sensor like no other you've used! The sensor contains a very tiny invisible laser source, and a matching sensor. The VL53L0X can detect the "time of flight", or how long the light has taken to bounce back to the sensor. Since it uses a very narrow light source, it is good for determining distance of only the surface directly in front of it. Unlike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
